// Logisim project CircuitoLuzesAEP.circ as structural Verilog
module Luzes (
  input  Dia1_7,
  input  Dias_3antesabate,
  input  OutrosDias,
  output Lampadas100Porcento,
  output Lampadas100PorcentoDesliga22hLiga4H,
  output Lampadas15Porcento,
  output Erro
);

  wire and_4_out, and_5_out, and_6_out, and_7_out, not_1_out, not_2_out, not_3_out, not_4_out, not_5_out,
       not_6_out, not_7_out, not_8_out, not_9_out;

  not not_1 (not_1_out, Dias_3antesabate);
  not not_2 (not_2_out, OutrosDias);
  not not_3 (not_3_out, Dia1_7);
  not not_4 (not_4_out, Dias_3antesabate);
  not not_5 (not_5_out, Dia1_7);
  not not_6 (not_6_out, OutrosDias);
  not not_7 (not_7_out, Dia1_7);
  not not_8 (not_8_out, Dias_3antesabate);
  not not_9 (not_9_out, OutrosDias);
  and and_1 (Lampadas100Porcento, Dia1_7, not_1_out, not_2_out);
  and and_2 (Lampadas100PorcentoDesliga22hLiga4H, not_3_out, not_4_out, OutrosDias);
  and and_3 (Lampadas15Porcento, not_5_out, Dias_3antesabate, not_6_out);
  and and_4 (and_4_out, not_7_out, not_8_out, not_9_out);
  and and_5 (and_5_out, Dias_3antesabate, OutrosDias);
  and and_6 (and_6_out, Dia1_7, OutrosDias);
  and and_7 (and_7_out, Dia1_7, Dias_3antesabate);
  or or_1 (Erro, and_4_out, and_5_out, and_6_out, and_7_out);
endmodule
