// Logisim project TemperaturaAEP.circ as structural Verilog
module ContTemperatura (
  input  TemperaturaMaior,
  input  TemperaturaMenor,
  output Aquecedores,
  output Resfriadores,
  output ERRO
);

  wire not_1_out, not_2_out;

  not not_1 (not_1_out, TemperaturaMaior);
  not not_2 (not_2_out, TemperaturaMenor);
  and and_1 (ERRO, TemperaturaMaior, TemperaturaMenor);
  and and_2 (Aquecedores, not_1_out, TemperaturaMenor);
  and and_3 (Resfriadores, TemperaturaMaior, not_2_out);
endmodule
