// Logisim project UmidadeAEP.circ as structural Verilog
module Umidade (
  input  UmidadeMaior,
  input  UmidadeMenor,
  output Exaustores,
  output Nebulizadores,
  output Erro
);

  wire not_1_out, not_2_out;

  not not_1 (not_1_out, UmidadeMenor);
  not not_2 (not_2_out, UmidadeMaior);
  and and_1 (Erro, UmidadeMaior, UmidadeMenor);
  and and_2 (Exaustores, UmidadeMaior, not_1_out);
  and and_3 (Nebulizadores, not_2_out, UmidadeMenor);
endmodule
